// Logisim project BellBox(8-bit computer).circ as structural Verilog
module FullAdder (
  input  in_1,
  input  in_2,
  input  in_3,
  output Sum,
  output out_5
);

  wire and_1_out, and_2_out, xor_1_out;

  xor xor_1 (xor_1_out, in_1, in_2);
  and and_1 (and_1_out, in_1, in_2);
  xor xor_2 (Sum, xor_1_out, in_3);
  and and_2 (and_2_out, in_3, xor_1_out);
  or or_1 (out_5, and_2_out, and_1_out);
endmodule

module ALU (
  input  [7:0] A,
  input  [7:0] B,
  input  [2:0] Controlbit,
  input  [7:0] incanddec,
  output [7:0] Output,
  output zero,
  output negative_flag,
  output overflow_flag,
  output carry
);

  wire adder_1_cout, adder_2_cout, subtractor_1_bout, subtractor_2_bout;
  wire [7:0] adder_1_out, adder_2_out, AND_out, NOT_out, OR_out, subtractor_1_out, subtractor_2_out, XOR_out;

  Adder adder_1 (.a(A), .b(B), .out(adder_1_out), .cout(adder_1_cout));  // open: cin
  Subtractor subtractor_1 (.a(A), .b(B), .out(subtractor_1_out), .bout(subtractor_1_bout));  // open: bin
  assign AND_out = A & B;  // AND_Gate AND, 8 bits wide
  assign OR_out = A | B;  // OR_Gate OR, 8 bits wide
  assign NOT_out = ~A;  // NOT_Gate NOT, 8 bits wide
  Adder adder_2 (.a(A), .b(incanddec), .out(adder_2_out), .cout(adder_2_cout));  // open: cin
  Subtractor subtractor_2 (.a(A), .b(incanddec), .out(subtractor_2_out), .bout(subtractor_2_bout));  // open: bin
  assign XOR_out = A ^ B;  // XOR_Gate XOR, 8 bits wide
  Multiplexer #(.select(3), .width(8), .enable("false")) multiplexer_1 (
    .in0(adder_1_out), .in1(subtractor_1_out), .in2(AND_out), .in3(OR_out), .in4(NOT_out), .in5(adder_2_out),
    .in6(subtractor_2_out), .in7(XOR_out), .out({negative_flag, Output[6:0]}), .sel(Controlbit));
  nor nor_1 (zero, Output[0], Output[1], Output[2], Output[3], Output[4], Output[5], Output[6], negative_flag);
  ExactlyOne xor_2 (.out(overflow_flag), .in0(negative_flag), .in1(B[7]), .in2(A[7]));
  or or_2 (carry, subtractor_1_bout, adder_1_cout, adder_2_cout, subtractor_2_bout);

  assign Output[7] = negative_flag;
endmodule

module Adder8bit (
  input  [7:0] A,
  input  Carry_In,
  input  [7:0] B,
  output [7:0] Sum,
  output out_5
);

  wire fulladder_1_out_5, fulladder_2_out_5, fulladder_3_out_5, fulladder_4_out_5, fulladder_5_out_5,
       fulladder_6_out_5, fulladder_7_out_5;

  FullAdder fulladder_1 (.in_1(A[0]), .in_2(B[0]), .in_3(Carry_In), .Sum(Sum[0]), .out_5(fulladder_1_out_5));
  FullAdder fulladder_2 (.in_1(A[1]), .in_2(B[1]), .in_3(fulladder_1_out_5), .Sum(Sum[1]), .out_5(fulladder_2_out_5));
  FullAdder fulladder_3 (.in_1(A[2]), .in_2(B[2]), .in_3(fulladder_2_out_5), .Sum(Sum[2]), .out_5(fulladder_3_out_5));
  FullAdder fulladder_4 (.in_1(A[3]), .in_2(B[3]), .in_3(fulladder_3_out_5), .Sum(Sum[3]), .out_5(fulladder_4_out_5));
  FullAdder fulladder_5 (.in_1(A[4]), .in_2(B[4]), .in_3(fulladder_4_out_5), .Sum(Sum[4]), .out_5(fulladder_5_out_5));
  FullAdder fulladder_6 (.in_1(A[5]), .in_2(B[5]), .in_3(fulladder_5_out_5), .Sum(Sum[5]), .out_5(fulladder_6_out_5));
  FullAdder fulladder_7 (.in_1(A[6]), .in_2(B[6]), .in_3(fulladder_6_out_5), .Sum(Sum[6]), .out_5(fulladder_7_out_5));
  FullAdder fulladder_8 (.in_1(A[7]), .in_2(B[7]), .in_3(fulladder_7_out_5), .Sum(Sum[7]), .out_5(out_5));
endmodule

module Subtractor8bit (
  input  [7:0] A,
  input  [7:0] B,
  output [7:0] Diff
);

  Subtractor subtractor_1 (.a(A), .b(B), .out(Diff));  // open: bin, bout
endmodule

module d_flip_flop (
  input  in_1,
  output out_2,
  output out_3
);

  wire clock_1_out, nand_1_out, nand_2_out, not_1_out;

  Clock #(.highDuration(2), .lowDuration(2)) clock_1 (.out(clock_1_out));
  not not_1 (not_1_out, in_1);
  nand nand_1 (nand_1_out, in_1, clock_1_out);
  nand nand_2 (nand_2_out, not_1_out, clock_1_out);
  nand nand_3 (out_2, nand_1_out, out_3);
  nand nand_4 (out_3, out_2, nand_2_out);
endmodule

module _1bitregister (
  input  load,
  input  data,
  input  enable,
  output out_4,
  output out_5
);

  wire and_1_out, and_2_out, d_flip_flop_1_out_2, not_1_out, or_1_out;

  not not_1 (not_1_out, load);
  and and_1 (and_1_out, out_4, not_1_out);
  and and_2 (and_2_out, load, data);
  or or_1 (or_1_out, and_1_out, and_2_out);
  d_flip_flop d_flip_flop_1 (.in_1(or_1_out), .out_2(d_flip_flop_1_out_2), .out_3(out_5));
  and and_3 (out_4, d_flip_flop_1_out_2, enable);

  // Notes on the sheet:
  //   D-flip flop
  //   Trisate Buffer
endmodule

module _8bitregister (
  input  [7:0] in_1,
  input  Enable,
  input  Load,
  output out_4,
  output out_5,
  output out_6,
  output [7:0] out_7,
  output out_8,
  output out_9,
  output out_10,
  output out_11,
  output out_12
);

  _1bitregister u_1bitregister_1 (.load(Load), .data(in_1[7]), .enable(Enable), .out_4(out_4));  // open: out_5
  _1bitregister u_1bitregister_2 (.load(Load), .data(in_1[6]), .enable(Enable), .out_4(out_5));  // open: out_5
  _1bitregister u_1bitregister_3 (.load(Load), .data(in_1[5]), .enable(Enable), .out_4(out_6));  // open: out_5
  _1bitregister u_1bitregister_4 (.load(Load), .data(in_1[4]), .enable(Enable), .out_4(out_7[4]));  // open: out_5
  _1bitregister u_1bitregister_5 (.load(Load), .data(in_1[3]), .enable(Enable), .out_4(out_7[3]));  // open: out_5
  _1bitregister u_1bitregister_6 (.load(Load), .data(in_1[2]), .enable(Enable), .out_4(out_7[2]));  // open: out_5
  _1bitregister u_1bitregister_7 (.load(Load), .data(in_1[1]), .enable(Enable), .out_4(out_7[1]));  // open: out_5
  _1bitregister u_1bitregister_8 (.load(Load), .data(in_1[0]), .enable(Enable), .out_4(out_7[0]));  // open: out_5

  assign out_7[7:5] = {out_4, out_5, out_6};
  assign out_8 = out_7[4];
  assign out_9 = out_7[3];
  assign out_10 = out_7[2];
  assign out_11 = out_7[1];
  assign out_12 = out_7[0];
endmodule

module _8bitinstructionregister (
  input  Enable,
  input  Load,
  input  [7:0] in_3,
  output [3:0] for_decoder,
  output [3:0] out_5
);

  _8bitregister u_8bitregister_1 (
    .in_1(in_3), .Enable(Enable), .Load(Load), .out_4(for_decoder[3]), .out_5(for_decoder[2]),
    .out_6(for_decoder[1]), .out_8(for_decoder[0]), .out_9(out_5[3]), .out_10(out_5[2]), .out_11(out_5[1]),
    .out_12(out_5[0]));  // open: out_7
endmodule
